# Fritzing sketch esp (saved by Fritzing 0.9.3b)
breadboards: 1

parts:
  U3 = NodeMCU V1.0
  DHT1 = DHT11 Humitidy and Temperature Sensor (3 pins)

nets:
  N1: U3.D4, DHT1.DATA
  3V3: U3.3V3, DHT1.VDD
  GND: U3.GND, DHT1.GND

custom parts:
  NodeMCU V1.0: ESP8266 based NodeMCU
  DHT11 Humitidy and Temperature Sensor (3 pins): DHT11 Humidity and Temperature Sensor (3 pins) from the design created by John De Cristofaro for Adafruit Industries.
